# Fritzing sketch Gravar FTDI ESP01 (saved by Fritzing 0.9.3b)
breadboards: 1

parts:
  Componente1 = Adafruit FTDI Friend [part_number="Adafruit #284"]
  U1 = ESP8266 WiFi Module [part_number=ESP8266]
  S1 = Pushbutton [package="[SMD]"]

nets:
  GND: Componente1.GND, U1.GND, S1.Pin_3, S1.Pin_4
  VCC: Componente1.VCC, U1.VCC
  N1: Componente1.TX, U1.TXD
  N2: Componente1.RX, U1.RXD
  N3: U1.GPIO_0, S1.Pin_1, S1.Pin_2

notes:
  Lembrando de colocar o FTDI com saida 3.3V
  Legenda de Cores:
  Vermelho:VCC
  Preto:GND
  Azul:RX
  Verde:TX
  Roxo:GPIO0

custom parts:
  Adafruit FTDI Friend: Long gone are the days of parallel ports and serial ports. Now the USB port reigns supreme! But USB is hard, and you just want to transfer your every-day serial data from a microcontroller to computer. What now? Enter the FTDI Friend! The FTDI Friend is a tweaked out FTDI FT232RL chip adapter. Sure, like the well-known FTDI cable, it can provide power to your project and there are 4 signal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
  ESP8266 WiFi Module: Generic WiFi Module based on the ESP8266 with onboard PCB antenna and UART communications
